// Logisim project logisim_computer.circ as structural Verilog
module NAND (
  input  in_1,
  input  in_2,
  output out_3
);

  nand nand_1 (out_3, in_1, in_2);
endmodule

module NOT (
  input  in_1,
  output out_2
);

  NAND nand_1 (.in_1(in_1), .in_2(in_1), .out_3(out_2));
endmodule

module AND (
  input  in_1,
  input  in_2,
  output out_3
);

  wire nand_1_out_3;

  NAND nand_1 (.in_1(in_1), .in_2(in_2), .out_3(nand_1_out_3));
  NOT not_1 (.in_1(nand_1_out_3), .out_2(out_3));
endmodule

module OR (
  input  in_1,
  input  in_2,
  output out_3
);

  wire nor_1_out_3;

  NOR nor_1 (.in_1(in_1), .in_2(in_2), .out_3(nor_1_out_3));
  NOT not_1 (.in_1(nor_1_out_3), .out_2(out_3));
endmodule

module XOR (
  input  in_1,
  input  in_2,
  output out_3
);

  wire and_1_out_3, not_1_out_2, or_1_out_3;

  AND and_1 (.in_1(in_1), .in_2(in_2), .out_3(and_1_out_3));
  OR or_1 (.in_1(in_1), .in_2(in_2), .out_3(or_1_out_3));
  NOT not_1 (.in_1(and_1_out_3), .out_2(not_1_out_2));
  AND and_2 (.in_1(or_1_out_3), .in_2(not_1_out_2), .out_3(out_3));
endmodule

module NOR (
  input  in_1,
  input  in_2,
  output out_3
);

  wire not_1_out_2, not_2_out_2;

  NOT not_1 (.in_1(in_1), .out_2(not_1_out_2));
  NOT not_2 (.in_1(in_2), .out_2(not_2_out_2));
  AND and_1 (.in_1(not_1_out_2), .in_2(not_2_out_2), .out_3(out_3));
endmodule

module NXOR (
  input  in_1,
  input  in_2,
  output out_3
);

  wire xor_1_out_3;

  XOR xor_1 (.in_1(in_1), .in_2(in_2), .out_3(xor_1_out_3));
  NOT not_1 (.in_1(xor_1_out_3), .out_2(out_3));
endmodule

module Half_Adder (
  input  x,
  input  y,
  output R,
  output U
);

  XOR xor_1 (.in_1(x), .in_2(y), .out_3(R));
  AND and_1 (.in_1(x), .in_2(y), .out_3(U));
endmodule

module Full_Adder (
  input  c,
  input  x,
  input  y,
  output R,
  output U
);

  wire half_adder_1_u, half_adder_2_r, half_adder_2_u;

  Half_Adder half_adder_1 (.x(c), .y(half_adder_2_r), .R(R), .U(half_adder_1_u));
  Half_Adder half_adder_2 (.x(x), .y(y), .R(half_adder_2_r), .U(half_adder_2_u));
  OR or_1 (.in_1(half_adder_1_u), .in_2(half_adder_2_u), .out_3(U));
endmodule

module _8_Bit_Adder (
  input  x0,
  input  y0,
  input  x1,
  input  y1,
  input  x2,
  input  y2,
  input  x3,
  input  y3,
  input  x4,
  input  y4,
  input  x5,
  input  y5,
  input  x6,
  input  y6,
  input  x7,
  input  y7,
  output _0,
  output _1,
  output _2,
  output _3,
  output _4,
  output _5,
  output _6,
  output _7,
  output overflow
);

  wire full_adder_1_u, full_adder_2_u, full_adder_3_u, full_adder_4_u, full_adder_5_u, full_adder_6_u,
       half_adder_1_u;

  Half_Adder half_adder_1 (.x(x0), .y(y0), .R(_0), .U(half_adder_1_u));
  Full_Adder full_adder_1 (.c(half_adder_1_u), .x(x1), .y(y1), .R(_1), .U(full_adder_1_u));
  Full_Adder full_adder_2 (.c(full_adder_1_u), .x(x2), .y(y2), .R(_2), .U(full_adder_2_u));
  Full_Adder full_adder_3 (.c(full_adder_2_u), .x(x3), .y(y3), .R(_3), .U(full_adder_3_u));
  Full_Adder full_adder_4 (.c(full_adder_3_u), .x(x4), .y(y4), .R(_4), .U(full_adder_4_u));
  Full_Adder full_adder_5 (.c(full_adder_4_u), .x(x5), .y(y5), .R(_5), .U(full_adder_5_u));
  Full_Adder full_adder_6 (.c(full_adder_5_u), .x(x6), .y(y6), .R(_6), .U(full_adder_6_u));
  Full_Adder full_adder_7 (.c(full_adder_6_u), .x(x7), .y(y7), .R(_7), .U(overflow));
endmodule

module Flip_Flop (
  input  Set,
  input  Reset,
  output State
);

  wire nor_1_out_3;

  NOR nor_1 (.in_1(Set), .in_2(State), .out_3(nor_1_out_3));
  NOR nor_2 (.in_1(nor_1_out_3), .in_2(Reset), .out_3(State));
endmodule

module D_Latch (
  input  Input,
  input  Write_Enable,
  input  Read_Enable,
  output out_4
);

  wire and_1_out_3, and_2_out_3, flip_flop_1_state, not_1_out_2;

  AND and_1 (.in_1(Input), .in_2(Write_Enable), .out_3(and_1_out_3));
  NOT not_1 (.in_1(Input), .out_2(not_1_out_2));
  AND and_2 (.in_1(not_1_out_2), .in_2(Write_Enable), .out_3(and_2_out_3));
  Flip_Flop flip_flop_1 (.Set(and_1_out_3), .Reset(and_2_out_3), .State(flip_flop_1_state));
  AND and_3 (.in_1(flip_flop_1_state), .in_2(Read_Enable), .out_3(out_4));
endmodule

module _256_Bit_Memory_Block (
  input  Write_Value,
  input  Read_Write
);

  Demultiplexer_16_out demultiplexer_16_out_1 ();  // open: Bit_0, Bit_1, Bit_2, Bit_3, _0, _1, _2, _3, _4, _5, _6, _7, _8, _9, _10, _11, _12, _13, _14, _15
  D_Latch_Selector d_latch_selector_1 ();  // open: Write_Value, Read_Write, Selector_1, Selector_2, Read_Value
  D_Latch_Selector d_latch_selector_2 ();  // open: Write_Value, Read_Write, Selector_1, Selector_2, Read_Value
  D_Latch_Selector d_latch_selector_3 ();  // open: Write_Value, Read_Write, Selector_1, Selector_2, Read_Value
  D_Latch_Selector d_latch_selector_4 ();  // open: Write_Value, Read_Write, Selector_1, Selector_2, Read_Value
  D_Latch_Selector d_latch_selector_5 ();  // open: Write_Value, Read_Write, Selector_1, Selector_2, Read_Value
  D_Latch_Selector d_latch_selector_6 ();  // open: Write_Value, Read_Write, Selector_1, Selector_2, Read_Value
  D_Latch_Selector d_latch_selector_7 ();  // open: Write_Value, Read_Write, Selector_1, Selector_2, Read_Value
  D_Latch_Selector d_latch_selector_8 ();  // open: Write_Value, Read_Write, Selector_1, Selector_2, Read_Value
  Demultiplexer_16_out demultiplexer_16_out_2 ();  // open: Bit_0, Bit_1, Bit_2, Bit_3, _0, _1, _2, _3, _4, _5, _6, _7, _8, _9, _10, _11, _12, _13, _14, _15
  D_Latch_Selector d_latch_selector_9 ();  // open: Write_Value, Read_Write, Selector_1, Selector_2, Read_Value
  D_Latch_Selector d_latch_selector_10 ();  // open: Write_Value, Read_Write, Selector_1, Selector_2, Read_Value
  D_Latch_Selector d_latch_selector_11 ();  // open: Write_Value, Read_Write, Selector_1, Selector_2, Read_Value
  D_Latch_Selector d_latch_selector_12 ();  // open: Write_Value, Read_Write, Selector_1, Selector_2, Read_Value
  D_Latch_Selector d_latch_selector_13 ();  // open: Write_Value, Read_Write, Selector_1, Selector_2, Read_Value
  D_Latch_Selector d_latch_selector_14 ();  // open: Write_Value, Read_Write, Selector_1, Selector_2, Read_Value
  D_Latch_Selector d_latch_selector_15 ();  // open: Write_Value, Read_Write, Selector_1, Selector_2, Read_Value
  D_Latch_Selector d_latch_selector_16 ();  // open: Write_Value, Read_Write, Selector_1, Selector_2, Read_Value
  D_Latch_Selector d_latch_selector_17 ();  // open: Write_Value, Read_Write, Selector_1, Selector_2, Read_Value
  D_Latch_Selector d_latch_selector_18 ();  // open: Write_Value, Read_Write, Selector_1, Selector_2, Read_Value
  D_Latch_Selector d_latch_selector_19 ();  // open: Write_Value, Read_Write, Selector_1, Selector_2, Read_Value
  D_Latch_Selector d_latch_selector_20 ();  // open: Write_Value, Read_Write, Selector_1, Selector_2, Read_Value
  D_Latch_Selector d_latch_selector_21 ();  // open: Write_Value, Read_Write, Selector_1, Selector_2, Read_Value
  D_Latch_Selector d_latch_selector_22 ();  // open: Write_Value, Read_Write, Selector_1, Selector_2, Read_Value
  D_Latch_Selector d_latch_selector_23 ();  // open: Write_Value, Read_Write, Selector_1, Selector_2, Read_Value
  D_Latch_Selector d_latch_selector_24 ();  // open: Write_Value, Read_Write, Selector_1, Selector_2, Read_Value
  D_Latch_Selector d_latch_selector_25 ();  // open: Write_Value, Read_Write, Selector_1, Selector_2, Read_Value
  D_Latch_Selector d_latch_selector_26 ();  // open: Write_Value, Read_Write, Selector_1, Selector_2, Read_Value
  D_Latch_Selector d_latch_selector_27 ();  // open: Write_Value, Read_Write, Selector_1, Selector_2, Read_Value
  D_Latch_Selector d_latch_selector_28 ();  // open: Write_Value, Read_Write, Selector_1, Selector_2, Read_Value
  D_Latch_Selector d_latch_selector_29 ();  // open: Write_Value, Read_Write, Selector_1, Selector_2, Read_Value
  D_Latch_Selector d_latch_selector_30 ();  // open: Write_Value, Read_Write, Selector_1, Selector_2, Read_Value
  D_Latch_Selector d_latch_selector_31 ();  // open: Write_Value, Read_Write, Selector_1, Selector_2, Read_Value
  D_Latch_Selector d_latch_selector_32 ();  // open: Write_Value, Read_Write, Selector_1, Selector_2, Read_Value
endmodule

module Demultiplexer_16_out (
  input  Bit_0,
  input  Bit_1,
  input  Bit_2,
  input  Bit_3,
  output _0,
  output _1,
  output _2,
  output _3,
  output _4,
  output _5,
  output _6,
  output _7,
  output _8,
  output _9,
  output _10,
  output _11,
  output _12,
  output _13,
  output _14,
  output _15
);

  wire _0_2_out_3, _0_out_3, _1_out_3, _2_out_3, _3_out_3, _4_out_3, _8_out_3, _12_out_3, not_1_out_2,
       not_2_out_2, not_3_out_2, not_4_out_2;

  NOT not_1 (.in_1(Bit_0), .out_2(not_1_out_2));
  NOT not_2 (.in_1(Bit_1), .out_2(not_2_out_2));
  NOT not_3 (.in_1(Bit_2), .out_2(not_3_out_2));
  NOT not_4 (.in_1(Bit_3), .out_2(not_4_out_2));
  AND u__0 (.in_1(not_1_out_2), .in_2(not_2_out_2), .out_3(_0_out_3));
  AND u__1 (.in_1(Bit_0), .in_2(not_2_out_2), .out_3(_1_out_3));
  AND u__2 (.in_1(not_1_out_2), .in_2(Bit_1), .out_3(_2_out_3));
  AND u__3 (.in_1(Bit_0), .in_2(Bit_1), .out_3(_3_out_3));
  AND _0_2 (.in_1(not_3_out_2), .in_2(not_4_out_2), .out_3(_0_2_out_3));
  AND u__4 (.in_1(Bit_2), .in_2(not_4_out_2), .out_3(_4_out_3));
  AND u__8 (.in_1(not_3_out_2), .in_2(Bit_3), .out_3(_8_out_3));
  AND u__12 (.in_1(Bit_2), .in_2(Bit_3), .out_3(_12_out_3));
  AND and_1 (.in_1(_0_out_3), .in_2(_0_2_out_3), .out_3(_0));
  AND and_2 (.in_1(_1_out_3), .in_2(_0_2_out_3), .out_3(_1));
  AND and_3 (.in_1(_2_out_3), .in_2(_0_2_out_3), .out_3(_2));
  AND and_4 (.in_1(_3_out_3), .in_2(_0_2_out_3), .out_3(_3));
  AND and_5 (.in_1(_0_out_3), .in_2(_4_out_3), .out_3(_4));
  AND and_6 (.in_1(_1_out_3), .in_2(_4_out_3), .out_3(_5));
  AND and_7 (.in_1(_2_out_3), .in_2(_4_out_3), .out_3(_6));
  AND and_8 (.in_1(_3_out_3), .in_2(_4_out_3), .out_3(_7));
  AND and_9 (.in_1(_0_out_3), .in_2(_8_out_3), .out_3(_8));
  AND and_10 (.in_1(_1_out_3), .in_2(_8_out_3), .out_3(_9));
  AND and_11 (.in_1(_2_out_3), .in_2(_8_out_3), .out_3(_10));
  AND and_12 (.in_1(_3_out_3), .in_2(_8_out_3), .out_3(_11));
  AND and_13 (.in_1(_0_out_3), .in_2(_12_out_3), .out_3(_12));
  AND and_14 (.in_1(_1_out_3), .in_2(_12_out_3), .out_3(_13));
  AND and_15 (.in_1(_2_out_3), .in_2(_12_out_3), .out_3(_14));
  AND and_16 (.in_1(_3_out_3), .in_2(_12_out_3), .out_3(_15));
endmodule

module D_Latch_Selector (
  input  Write_Value,
  input  Read_Write,
  input  Selector_1,
  input  Selector_2,
  output Read_Value
);

  wire and_1_out_3, and_2_out_3, and_3_out_3, not_1_out_2;

  AND and_1 (.in_1(Selector_1), .in_2(Selector_2), .out_3(and_1_out_3));
  AND and_2 (.in_1(and_1_out_3), .in_2(Read_Write), .out_3(and_2_out_3));
  AND and_3 (.in_1(and_1_out_3), .in_2(not_1_out_2), .out_3(and_3_out_3));
  NOT not_1 (.in_1(Read_Write), .out_2(not_1_out_2));
  D_Latch d_latch_1 (.Input(Write_Value), .Write_Enable(and_2_out_3), .Read_Enable(and_3_out_3), .out_4(Read_Value));
endmodule
